// Logisim project TinyCPU-FetchDecode.circ as structural Verilog: 1 circuit, main circuit FetchDecode
module FetchDecode (
  input  DEC_JUMP_NOT_ZERO,
  input  NOT_ZERO,
  input  CLK,
  input  RESET,
  input  [15:0] PROGRAM_LIMIT,
  input  DEC_HALT_ERROR,
  output JUMP_NOT_ZERO,
  output HALT_ERROR,
  output [11:0] PC_OUT,
  output [21:0] OPCODE
);

  wire PC_RANGE_eq;
  wire [15:0] PC_INCREMENT_out;
  wire [15:12] PC_q;

  Register #(.width(16)) PC (.D(PC_INCREMENT_out), .clk(CLK), .Q({PC_q, PC_OUT}), .clr(RESET));  // open: en
  Comparator #(.width(16)) PC_RANGE (.a(PROGRAM_LIMIT), .b({PC_q, PC_OUT}), .eq(PC_RANGE_eq));  // open: gt, lt
  Adder #(.width(16)) PC_INCREMENT (.a({PC_q, PC_OUT}), .b({16{1'b1}}), .out(PC_INCREMENT_out));  // open: cin, cout
  ROM #(.addrWidth(12), .dataWidth(22)) INSTRUCTION_ROM (.addr(PC_OUT), .data(OPCODE));
  and JNZ_TAKEN (JUMP_NOT_ZERO, DEC_JUMP_NOT_ZERO, NOT_ZERO);
  or ERROR_HALT (HALT_ERROR, PC_RANGE_eq, DEC_HALT_ERROR);

  // Notes on the sheet:
  //   PROGRAM_LIMIT: initial=0xfff
  //   AP 7 machine format v1: stable six-bit opcode allocation and encoder-generated ROM
  //   contents of INSTRUCTION_ROM (hex, n*v repeats v):
  //   00ffff 1c0065 000003 1c0064 2a0000 050065 1c0064 240004 2c0000
endmodule
